# Fritzing sketch pathfinder (saved by Fritzing 1.0.5)
breadboards: 1

parts:
  ESP32_PICO_KIT_v1 = ESP32 PICO KIT [package="DIP (Dual Inline) [THT]"]
  NEOPIXEL4 = Neopixel Strip -- White (60/m) [part_number=1138]
  J3 = Basic Servo
  Bauteil3 = InvenSense MPU6050
  PART1 = APDS-9960 RGB and Gesture Sensor [part_number=SEN-12787]  # not connected

nets:
  N1: ESP32_PICO_KIT_v1.GPIO_14, NEOPIXEL4.DI
  N2: ESP32_PICO_KIT_v1.GPIO_12, J3.pulse
  N3: ESP32_PICO_KIT_v1.3V, Bauteil3.VCC
  GND: ESP32_PICO_KIT_v1.GND, NEOPIXEL4.GND, J3.gnd, Bauteil3.GND
  5V: ESP32_PICO_KIT_v1.5V, NEOPIXEL4.+5V, J3.vcc
  N4: ESP32_PICO_KIT_v1.GPIO_22_/_SCL, Bauteil3.SCL
  N5: ESP32_PICO_KIT_v1.GPIO_21_/_SDA, Bauteil3.SDA

custom parts:
  ESP32 PICO KIT: ESP32-PICO-KIT is an ESP32-based mini development board produced by Espressif. The core of this board is ESP32-PICO-D4 - a System-in-Package (SiP) module with complete Wi-Fi and Bluetooth functionalities. Compared to other ESP32 modules, ESP32-PICO-D4 integrates the following peripheral components in one single package, which otherwise would need to be installed separately.
  Neopixel Strip -- White (60/m): Neopixel Strip, White, 60 pixels per meter.
  APDS-9960 RGB and Gesture Sensor: Breakout board for the Avago APDS-9960 proximity, light, RGB, and gesture sensors. Please visit www.sparkfun.com to learn more.
