# Fritzing sketch timers_v3 (saved by Fritzing 1.0.5)
breadboards: 1

parts:
  OLED1 = OLED 128x64 I2C Monochrome Display VDD-GND
  Bauteil1 = Arduino Nano (Rev3.0)
  ZS-042_RTC1 = ZS-042 RTC Module  # not connected
  Part3 = 12 NeoPixel Ring [part_number=1643]
  Bauteil2 = InvenSense MPU6050
  Bauteil4 = Adafruit VL53L0X Time of Flight Distance Sensor [part_number="Adafruit #3317"]
  J1 = Basic Servo

nets:
  VDD: OLED1.VDD, Bauteil1.3V3, Bauteil2.VCC, Bauteil2.AD0, Bauteil4.VIN
  GND: OLED1.GND, Bauteil1.GND, Part3.GND, Bauteil2.GND, Bauteil4.GND, J1.gnd
  N1: OLED1.SCK, Bauteil1.A5, Bauteil2.SCL, Bauteil4.SCL
  N2: OLED1.SDA, Bauteil1.A4, Bauteil2.SDA, Bauteil4.SDA
  N3: Bauteil1.D9, J1.pulse
  N4: Bauteil1.D10, Part3.IN
  5V: Bauteil1.5V, Part3.VDD, J1.vcc

custom parts:
  OLED 128x64 I2C Monochrome Display VDD-GND: OLED 128x64 I2C Monochrome Display. Note: there are two variants of this part, this one is the VDD GND SCK SDA variant. The other is GND VDD SCK SDA. Make sure you select the part that matches your module as using the incorrect part will probably destroy your module! In addition the mounting holes are marked on silkscreen but not by default drilled. If you want drilled mounting holes, copy a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
  12 NeoPixel Ring: 12 ultra bright smart LED NeoPixels are arranged in a circle with 1.5" (37mm) outer diameter. The rings are 'chainable' - connect the output pin of one to the input pin of another. Use only one microcontroller pin to control as many as you can chain together! Each LED is addressable as the driver chip is inside the LED. Each one has ~18mA constant current drive so the color will be very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
  Adafruit VL53L0X Time of Flight Distance Sensor: The VL53L0X is a Time of Flight distance sensor like no other you've used! The sensor contains a very tiny invisible laser source, and a matching sensor. The VL53L0X can detect the "time of flight", or how long the light has taken to bounce back to the sensor. Since it uses a very narrow light source, it is good for determining distance of only the surface directly in front of it. Unlike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
